// Logisim project CPU2.circ as structural Verilog: 24 circuits, main circuit main
module main (
  input  clk,
  input  rst,
  input  [31:0] Jin,
  input  Jen,
  output [31:0] Jout,
  output InstDone,
  output [31:0] R1,
  output [31:0] R2,
  output [31:0] R3,
  output [31:0] R4,
  output [31:0] R5,
  output [31:0] R6,
  output [31:0] R7,
  output [31:0] R8,
  output [31:0] R9,
  output [31:0] R10,
  output [31:0] R11,
  output [31:0] R12,
  output [31:0] R13,
  output [31:0] R14,
  output [31:0] R15,
  output [31:0] R16,
  output [31:0] R17,
  output [31:0] R18,
  output [31:0] R19,
  output [31:0] R20,
  output [31:0] R21,
  output [31:0] R22,
  output [31:0] R23,
  output [31:0] R24,
  output [31:0] R25,
  output [31:0] R26,
  output [31:0] R27,
  output [31:0] R28,
  output [31:0] R29,
  output [31:0] R30,
  output [31:0] R31
);

  wire ALUSrc, ALUSrc_ID, and_1_out, and_2_out, branch_taken, comparator_1_eq, comparator_2_eq,
       comparator_3_eq, donedivv, instdone_EX, instdone_ID, instdone_IF, instdone_MEM, isdivv, isdivv_ID,
       MemWrite, MemWrite_ID, MemWriteEX, not_2_out, resettt_s, SllHandle, SllHandle_ID, stallex;
  wire [1:0] ALUOp, ALUOp_ID, ALUOutSrc, ALUOutSrc_ID, MemToReg, MemToReg_EX, MemToReg_ID, MemToReg_MEM,
       PCSrc, RegDst, RegDst_ID;
  wire [3:0] opcodesaaz_1_aloup;
  wire [4:0] regd_EX, regd_ID, regs_EX, regs_ID, regt_EX, regt_ID, RF_WB_Dest, shamt_EX, writeDest_EX,
       writeDest_MEM;
  wire [4:3] shamt_ID;
  wire [5:0] funct_EX, funct_ID, opcode_EX, opcode_ID;
  wire [8:0] branch_adrs, pc_plus_one, pcout, PCTemp_EX, PCTemp_ID, PCTemp_MEM, PCTemp_WB, updatedpc;
  wire [8:6] J_Adrs;
  wire [31:0] aluoutt, alureg, ALUResultWB, aluuuuuu_1_res_high, Areg, bit_extender_1_out,
       bit_extender_3_out, bit_extender_4_out, Breg, d0, DataMem_dout, imm_sign_ext_EX, imm_sign_ext_ID,
       inputalu1, inputalu2, InstrMem_dout, memoryregoutput, MemWriteData, mfhii, mfloo, multiplexer_2_out,
       multiplexer_5_out, RF_Data_in, RF_rs, RF_rt;
  wire [31:9] adder_2_out;

  Register #(.width(1)) register_1 (.D(1'b1), .en(stallex), .clk(clk), .Q(instdone_IF), .clr(rst));
  Register #(.width(9)) pcccc (.D(updatedpc), .en(stallex), .clk(clk), .Q(pcout), .clr(rst));
  Adder #(.width(9)) adder_1 (.a(pcout), .b(9'h1), .out(pc_plus_one), .cin(1'b0));  // open: cout
  Multiplexer #(.select(2), .width(9)) multiplexer_1 (
    .in0(pc_plus_one), .in1(branch_adrs), .in2({J_Adrs, funct_ID}), .in3(RF_rs[8:0]), .out(updatedpc),
    .sel(PCSrc));
  memooory InstrMem (
    .Jin(Jin), .Din({32{1'b0}}), .Addr(pcout), .clk(clk), .Wen(1'b0), .Jen(Jen), .Jout(Jout),
    .Dout(InstrMem_dout));
  Register #(.width(1)) register_2 (.D(instdone_IF), .en(stallex), .clk(clk), .Q(instdone_ID), .clr(rst));
  Register #(.width(9)) PCTemp (.D(pc_plus_one), .en(stallex), .clk(clk), .Q(PCTemp_ID), .clr(rst));
  Register #(.width(32)) IF_ID_InstReg (
    .D(InstrMem_dout), .en(stallex), .clk(clk),
    .Q({opcode_ID, regs_ID, regt_ID, regd_ID, shamt_ID, J_Adrs, funct_ID}), .clr(rst));
  assign bit_extender_1_out = {{23{1'b0}}, PCTemp_ID};  // Bit_Extender bit_extender_1
  Adder #(.width(32)) adder_2 (
    .a(bit_extender_1_out), .b(imm_sign_ext_ID), .out({adder_2_out, branch_adrs}), .cin(1'b0));  // open: cout
  assign imm_sign_ext_ID = {{16{regd_ID[4]}}, {regd_ID, shamt_ID, J_Adrs, funct_ID}};  // Bit_Extender bit_extender_2
  not not_1 (branch_taken, comparator_1_eq);
  Comparator #(.width(32)) comparator_1 (.a(RF_rs), .b(RF_rt), .eq(comparator_1_eq));  // open: gt, lt
  regfillll regfillll_1 (
    .Read0(regs_ID), .Read1(regt_ID), .Write(RF_WB_Dest), .Data(RF_Data_in), .WriteReg(1'b1), .clk(clk),
    .rst(rst), .RegOut1(RF_rs), .RegOut2(RF_rt), .R0(d0), .R1(R1), .R2(R2), .R3(R3), .R4(R4), .R5(R5),
    .R6(R6), .R7(R7), .R8(R8), .R9(R9), .R10(R10), .R11(R11), .R12(R12), .R13(R13), .R14(R14), .R15(R15),
    .R16(R16), .R17(R17), .R18(R18), .R19(R19), .R20(R20), .R21(R21), .R22(R22), .R23(R23), .R24(R24),
    .R25(R25), .R26(R26), .R27(R27), .R28(R28), .R29(R29), .R30(R30), .R31(R31));
  Register #(.width(6)) register_3 (.D(opcode_ID), .en(stallex), .clk(clk), .Q(opcode_EX), .clr(rst));
  Register #(.width(5)) register_4 (.D(regs_ID), .en(stallex), .clk(clk), .Q(regs_EX), .clr(rst));
  Register #(.width(5)) register_5 (.D(regt_ID), .en(stallex), .clk(clk), .Q(regt_EX), .clr(rst));
  Register #(.width(5)) register_6 (.D(regd_ID), .en(stallex), .clk(clk), .Q(regd_EX), .clr(rst));
  Register #(.width(5)) register_7 (.D({shamt_ID, J_Adrs}), .en(stallex), .clk(clk), .Q(shamt_EX), .clr(rst));
  Register #(.width(6)) register_8 (.D(funct_ID), .en(stallex), .clk(clk), .Q(funct_EX), .clr(rst));
  Register #(.width(9)) register_9 (.D(PCTemp_ID), .en(stallex), .clk(clk), .Q(PCTemp_EX), .clr(rst));
  Register #(.width(1)) register_10 (.D(and_1_out), .en(1'b1), .clk(clk), .Q(instdone_EX), .clr(rst));
  and and_1 (and_1_out, instdone_ID, stallex);
  Register #(.width(2)) register_11 (.D(ALUOp_ID), .en(stallex), .clk(clk), .Q(ALUOp), .clr(rst));
  Register #(.width(1)) register_12 (.D(isdivv_ID), .en(stallex), .clk(clk), .Q(isdivv), .clr(rst));
  Register #(.width(1)) register_13 (.D(ALUSrc_ID), .en(stallex), .clk(clk), .Q(ALUSrc), .clr(rst));
  Register #(.width(2)) register_14 (.D(RegDst_ID), .en(stallex), .clk(clk), .Q(RegDst), .clr(rst));
  Register #(.width(2)) register_15 (.D(MemToReg_ID), .en(stallex), .clk(clk), .Q(MemToReg_EX), .clr(rst));
  Register #(.width(1)) register_16 (.D(MemWrite_ID), .en(stallex), .clk(clk), .Q(MemWriteEX), .clr(rst));
  Register #(.width(1)) register_17 (.D(SllHandle_ID), .en(stallex), .clk(clk), .Q(SllHandle), .clr(rst));
  Register #(.width(2)) register_18 (.D(ALUOutSrc_ID), .en(stallex), .clk(clk), .Q(ALUOutSrc), .clr(rst));
  Register #(.width(32)) A (.D(RF_rs), .en(stallex), .clk(clk), .Q(Areg), .clr(rst));
  Register #(.width(32)) B (.D(RF_rt), .en(stallex), .clk(clk), .Q(Breg), .clr(rst));
  Register #(.width(32)) register_19 (.D(imm_sign_ext_ID), .en(stallex), .clk(clk), .Q(imm_sign_ext_EX), .clr(rst));
  opcodesaaz opcodesaaz_1 (.ALUOp(ALUOp), .functt(funct_EX), .aloup(opcodesaaz_1_aloup));
  Comparator #(.width(5)) comparator_2 (.a(regs_EX), .b(RF_WB_Dest), .eq(comparator_2_eq));  // open: gt, lt
  Multiplexer #(.width(32)) multiplexer_2 (.in0(Breg), .in1(imm_sign_ext_EX), .out(multiplexer_2_out), .sel(ALUSrc));
  assign bit_extender_3_out = {{27{1'b0}}, shamt_EX};  // Bit_Extender bit_extender_3
  Comparator #(.width(5)) comparator_3 (.a(regt_EX), .b(writeDest_MEM), .eq(comparator_3_eq));  // open: gt, lt
  aluuuuuu aluuuuuu_1 (
    .b(inputalu2), .output_inc(1'b0), .a(inputalu1), .aluop(opcodesaaz_1_aloup), .output_inverted(1'b0),
    .clkk(clk), .rsstt(rst), .startdivvand(isdivv), .isdivv(isdivv), .res_low(aluoutt),
    .res_high(aluuuuuu_1_res_high), .done(donedivv));
  Multiplexer #(.width(32)) multiplexer_3 (.in0(Areg), .in1(Breg), .out(inputalu1), .sel(comparator_2_eq));
  Multiplexer #(.width(32)) multiplexer_4 (
    .in0(multiplexer_2_out), .in1(bit_extender_3_out), .out(inputalu2), .sel(comparator_3_eq));
  Register #(.width(32)) looo (.D(aluoutt), .en(isdivv), .clk(clk), .Q(mfloo), .clr(rst));
  Register #(.width(32)) hii (.D(aluuuuuu_1_res_high), .en(isdivv), .clk(clk), .Q(mfhii), .clr(rst));
  Multiplexer #(.select(2), .width(32)) multiplexer_5 (
    .in0(aluoutt), .in1(mfloo), .in2(mfhii), .out(multiplexer_5_out), .sel(ALUOutSrc));  // open: in3
  or or_1 (resettt_s, 1'b0, rst);
  Register #(.width(32)) ALUOutReg (.D(multiplexer_5_out), .en(1'b1), .clk(clk), .Q(alureg), .clr(resettt_s));
  D_Flip_Flop u_MemWrite (.D(and_2_out), .clk(clk), .Q(MemWrite), .preset(1'b0), .reset(resettt_s));  // open: Qn
  and and_2 (and_2_out, MemWriteEX, stallex);
  Register #(.width(32)) u_MemWriteData (.D(Breg), .en(1'b1), .clk(clk), .Q(MemWriteData), .clr(resettt_s));
  Register #(.width(5)) WriteDest (.D(writeDest_EX), .en(1'b1), .clk(clk), .Q(writeDest_MEM), .clr(resettt_s));
  Register #(.width(9)) register_20 (.D(PCTemp_EX), .en(1'b1), .clk(clk), .Q(PCTemp_MEM), .clr(resettt_s));
  Register #(.width(1)) register_21 (.D(instdone_EX), .en(1'b1), .clk(clk), .Q(instdone_MEM), .clr(resettt_s));
  Register #(.width(2)) register_22 (.D(MemToReg_EX), .en(1'b1), .clk(clk), .Q(MemToReg_MEM), .clr(resettt_s));
  Multiplexer #(.select(2), .width(5)) multiplexer_6 (
    .in0(regt_EX), .in1(regd_EX), .in2({5{1'b1}}), .in3({5{1'b0}}), .out(writeDest_EX), .sel(RegDst));
  memooory DataMem (
    .Jin(Jout), .Din(MemWriteData), .Addr(alureg[8:0]), .clk(clk), .Wen(MemWrite), .Jen(Jen),
    .Dout(DataMem_dout));  // open: Jout
  assign bit_extender_4_out = {{23{1'b0}}, PCTemp_WB};  // Bit_Extender bit_extender_4
  Register #(.width(32)) memorydataa (.D(DataMem_dout), .en(1'b1), .clk(clk), .Q(memoryregoutput), .clr(rst));
  Register #(.width(32)) ALUResult (.D(alureg), .en(1'b1), .clk(clk), .Q(ALUResultWB), .clr(rst));
  Register #(.width(5)) WB_Dest (.D(writeDest_MEM), .en(1'b1), .clk(clk), .Q(RF_WB_Dest), .clr(rst));
  Register #(.width(9)) register_23 (.D(PCTemp_MEM), .en(1'b1), .clk(clk), .Q(PCTemp_WB), .clr(rst));
  Register #(.width(1)) register_24 (.D(instdone_MEM), .en(1'b1), .clk(clk), .Q(InstDone), .clr(rst));
  Register #(.width(2)) register_25 (.D(MemToReg_MEM), .en(1'b1), .clk(clk), .Q(MemToReg), .clr(rst));
  Multiplexer #(.select(2), .width(32)) multiplexer_7 (
    .in0(ALUResultWB), .in1(memoryregoutput), .in2(bit_extender_4_out), .in3({32{1'b0}}), .out(RF_Data_in),
    .sel(MemToReg));
  CU cu_1 (
    .opcode(opcode_ID), .funct(funct_ID), .rsnamosavirt(branch_taken), .in_4(donedivv), .pcsrcc(PCSrc),
    .ALUOp(ALUOp_ID), .ALUOutSrc(ALUOutSrc_ID), .SllHandle(SllHandle_ID), .ALUSrc(ALUSrc_ID),
    .isdivv(isdivv_ID), .MemWrite(MemWrite_ID), .MemToReg(MemToReg_ID), .regdst(RegDst_ID));
  not not_2 (not_2_out, donedivv);
  nand nand_1 (stallex, isdivv, not_2_out);

  // Other names for the same wires on the sheet: J_Adrs[5:0] = funct_ID; shamt_ID[2:0] = J_Adrs; clockk = clk;
  //   d1[31:0] = R1; d2[31:0] = R2; d3[31:0] = R3; d4[31:0] = R4; d5[31:0] = R5; d6[31:0] = R6; d7[31:0] = R7;
  //   d8[31:0] = R8; d9[31:0] = R9; d10[31:0] = R10; d11[31:0] = R11; d12[31:0] = R12; d13[31:0] = R13;
  //   d14[31:0] = R14; d15[31:0] = R15; d16[31:0] = R16; d17[31:0] = R17; d18[31:0] = R18; d19[31:0] = R19;
  //   d20[31:0] = R20; d21[31:0] = R21; d22[31:0] = R22; d23[31:0] = R23; d24[31:0] = R24; d25[31:0] = R25;
  //   d26[31:0] = R26; d27[31:0] = R27; d28[31:0] = R28; d29[31:0] = R29; d30[31:0] = R30; d31[31:0] = R31;
  //   jeeen = Jen; jiin[31:0] = Jin; joutt[31:0] = Jout; resettt = rst

  // Notes on the sheet:
  //   Inputs
  //   IF
  //   IF/ID
  //   ID
  //   ID/EX
  //   EX
  //   EX/MEM
  //   MEM
  //   MEM/WB
endmodule

module CU (
  input  [5:0] opcode,
  input  [5:0] funct,
  input  rsnamosavirt,
  input  in_4,
  output [1:0] pcsrcc,
  output [1:0] ALUOp,
  output [1:0] ALUOutSrc,
  output SllHandle,
  output ALUSrc,
  output isdivv,
  output MemWrite,
  output [1:0] MemToReg,
  output [1:0] regdst
);

  wire and_1_out, and_2_out, bne, comparator_10_eq, comparator_11_eq, comparator_12_eq, comparator_13_eq,
       comparator_14_eq, isaddi, isbne, isj, isjal, isjr, islw, isrtype, isslti, not_1_out, not_2_out,
       or_4_out;

  Comparator #(.width(6)) comparator_1 (.a(opcode), .b(6'b000101), .eq(bne));  // open: gt, lt
  or or_1 (ALUSrc, isslti, islw, MemWrite, isaddi);
  or or_2 (ALUOp[0], isbne, isslti);
  or or_3 (ALUOp[1], isslti, isrtype);
  Comparator #(.width(6)) comparator_2 (.a(opcode), .b({6{1'b0}}), .eq(isrtype));  // open: gt, lt
  Comparator #(.width(6)) comparator_3 (.a(opcode), .b(6'b001000), .eq(isaddi));  // open: gt, lt
  Comparator #(.width(6)) comparator_4 (.a(opcode), .b(6'b100011), .eq(islw));  // open: gt, lt
  Comparator #(.width(6)) comparator_5 (.a(opcode), .b(6'b101011), .eq(MemWrite));  // open: gt, lt
  or or_4 (or_4_out, 1'b0, isjr, isj, isbne, MemWrite, isdivv);
  not not_1 (not_1_out, isjr);
  not not_2 (not_2_out, isdivv);
  and and_1 (and_1_out, isrtype, not_1_out, not_2_out);
  or or_5 (MemToReg[0], islw, or_4_out);
  or or_6 (regdst[0], and_1_out, or_4_out);
  or or_7 (regdst[1], or_4_out, isjal);
  Comparator #(.width(6)) comparator_6 (.a(opcode), .b(6'b000101), .eq(isbne));  // open: gt, lt
  Comparator #(.width(6)) comparator_7 (.a(opcode), .b(6'b001010), .eq(isslti));  // open: gt, lt
  Comparator #(.width(6)) comparator_8 (.a(opcode), .b(6'b000010), .eq(isj));  // open: gt, lt
  Comparator #(.width(6)) comparator_9 (.a(opcode), .b(6'b000011), .eq(isjal));  // open: gt, lt
  or or_8 (MemToReg[1], or_4_out, isjal);
  and and_2 (and_2_out, rsnamosavirt, isbne);
  Comparator #(.width(6)) comparator_10 (.a(funct), .b(6'b001000), .eq(comparator_10_eq));  // open: gt, lt
  Comparator #(.width(6)) comparator_11 (.a(funct), .b(6'b011010), .eq(comparator_11_eq));  // open: gt, lt
  Comparator #(.width(6)) comparator_12 (.a(funct), .b(6'b010000), .eq(comparator_12_eq));  // open: gt, lt
  Comparator #(.width(6)) comparator_13 (.a(funct), .b(6'b010010), .eq(comparator_13_eq));  // open: gt, lt
  Comparator #(.width(6)) comparator_14 (.a(funct), .b({6{1'b0}}), .eq(comparator_14_eq));  // open: gt, lt
  or or_9 (pcsrcc[0], and_2_out, isjr);
  or or_10 (pcsrcc[1], isjr, isj, isjal);
  and and_3 (isjr, comparator_10_eq, isrtype);
  and and_4 (isdivv, comparator_11_eq, isrtype);
  and and_5 (ALUOutSrc[1], comparator_12_eq, isrtype);
  and and_6 (ALUOutSrc[0], comparator_13_eq, isrtype);
  and and_7 (SllHandle, comparator_14_eq, isrtype);

  // Other names for the same wires on the sheet: ismflo = ALUOutSrc[0]; ismfhi = ALUOutSrc[1]; donedivv = in_4;
  //   issw = MemWrite; op_low[2:0] = opcode[2:0]; op_high[2:0] = opcode[5:3]; rsnotrt = rsnamosavirt
endmodule

module RAM_16Word (
  input  [31:0] Jin,
  input  [31:0] Din,
  input  [3:0] Addr,
  input  clk,
  input  Wen,
  input  Jen,
  output [31:0] Jout,
  output [31:0] Dout
);

  wire decd0, decd1, decd2, decd3, decd4, decd5, decd6, decd7, decd8, decd9, decd10, decd11, decd12, decd13,
       decd14, decd15, or_1_out, or_2_out, or_3_out, or_4_out, or_5_out, or_6_out, or_7_out, or_8_out,
       or_9_out, or_10_out, or_11_out, or_12_out, or_13_out, or_14_out, or_15_out, or_16_out;
  wire [31:0] multiplexer_1_out, multiplexer_2_out, multiplexer_3_out, multiplexer_4_out, multiplexer_5_out,
       multiplexer_6_out, multiplexer_7_out, multiplexer_8_out, multiplexer_9_out, multiplexer_10_out,
       multiplexer_11_out, multiplexer_12_out, multiplexer_13_out, multiplexer_14_out, multiplexer_15_out,
       multiplexer_16_out, register_1_q, register_2_q, register_3_q, register_4_q, register_5_q,
       register_6_q, register_7_q, register_8_q, register_9_q, register_10_q, register_11_q, register_12_q,
       register_13_q, register_14_q, register_15_q;

  Multiplexer #(.width(32)) multiplexer_1 (.in0(Din), .in1(Jin), .out(multiplexer_1_out), .sel(Jen));
  Multiplexer #(.width(32)) multiplexer_2 (.in0(Din), .in1(register_1_q), .out(multiplexer_2_out), .sel(Jen));
  Multiplexer #(.width(32)) multiplexer_3 (.in0(Din), .in1(register_2_q), .out(multiplexer_3_out), .sel(Jen));
  Multiplexer #(.width(32)) multiplexer_4 (.in0(Din), .in1(register_3_q), .out(multiplexer_4_out), .sel(Jen));
  Multiplexer #(.width(32)) multiplexer_5 (.in0(Din), .in1(register_4_q), .out(multiplexer_5_out), .sel(Jen));
  Multiplexer #(.width(32)) multiplexer_6 (.in0(Din), .in1(register_5_q), .out(multiplexer_6_out), .sel(Jen));
  Multiplexer #(.width(32)) multiplexer_7 (.in0(Din), .in1(register_6_q), .out(multiplexer_7_out), .sel(Jen));
  Multiplexer #(.width(32)) multiplexer_8 (.in0(Din), .in1(register_7_q), .out(multiplexer_8_out), .sel(Jen));
  Multiplexer #(.width(32)) multiplexer_9 (.in0(Din), .in1(register_8_q), .out(multiplexer_9_out), .sel(Jen));
  Multiplexer #(.width(32)) multiplexer_10 (.in0(Din), .in1(register_9_q), .out(multiplexer_10_out), .sel(Jen));
  Multiplexer #(.width(32)) multiplexer_11 (.in0(Din), .in1(register_10_q), .out(multiplexer_11_out), .sel(Jen));
  Multiplexer #(.width(32)) multiplexer_12 (.in0(Din), .in1(register_11_q), .out(multiplexer_12_out), .sel(Jen));
  Multiplexer #(.width(32)) multiplexer_13 (.in0(Din), .in1(register_12_q), .out(multiplexer_13_out), .sel(Jen));
  Multiplexer #(.width(32)) multiplexer_14 (.in0(Din), .in1(register_13_q), .out(multiplexer_14_out), .sel(Jen));
  Multiplexer #(.width(32)) multiplexer_15 (.in0(Din), .in1(register_14_q), .out(multiplexer_15_out), .sel(Jen));
  Multiplexer #(.width(32)) multiplexer_16 (.in0(Din), .in1(register_15_q), .out(multiplexer_16_out), .sel(Jen));
  Register #(.width(32)) register_1 (.D(multiplexer_1_out), .en(or_1_out), .clk(clk), .Q(register_1_q));  // open: clr
  or or_1 (or_1_out, Jen, decd0);
  Register #(.width(32)) register_2 (.D(multiplexer_2_out), .en(or_2_out), .clk(clk), .Q(register_2_q));  // open: clr
  or or_2 (or_2_out, Jen, decd1);
  Register #(.width(32)) register_3 (.D(multiplexer_3_out), .en(or_3_out), .clk(clk), .Q(register_3_q));  // open: clr
  or or_3 (or_3_out, Jen, decd2);
  Register #(.width(32)) register_4 (.D(multiplexer_4_out), .en(or_4_out), .clk(clk), .Q(register_4_q));  // open: clr
  or or_4 (or_4_out, Jen, decd3);
  Register #(.width(32)) register_5 (.D(multiplexer_5_out), .en(or_5_out), .clk(clk), .Q(register_5_q));  // open: clr
  or or_5 (or_5_out, Jen, decd4);
  Register #(.width(32)) register_6 (.D(multiplexer_6_out), .en(or_6_out), .clk(clk), .Q(register_6_q));  // open: clr
  or or_6 (or_6_out, Jen, decd5);
  Register #(.width(32)) register_7 (.D(multiplexer_7_out), .en(or_7_out), .clk(clk), .Q(register_7_q));  // open: clr
  or or_7 (or_7_out, Jen, decd6);
  Register #(.width(32)) register_8 (.D(multiplexer_8_out), .en(or_8_out), .clk(clk), .Q(register_8_q));  // open: clr
  or or_8 (or_8_out, Jen, decd7);
  Register #(.width(32)) register_9 (.D(multiplexer_9_out), .en(or_9_out), .clk(clk), .Q(register_9_q));  // open: clr
  or or_9 (or_9_out, Jen, decd8);
  Register #(.width(32)) register_10 (
    .D(multiplexer_10_out), .en(or_10_out), .clk(clk), .Q(register_10_q));  // open: clr
  or or_10 (or_10_out, Jen, decd9);
  Register #(.width(32)) register_11 (
    .D(multiplexer_11_out), .en(or_11_out), .clk(clk), .Q(register_11_q));  // open: clr
  or or_11 (or_11_out, Jen, decd10);
  Register #(.width(32)) register_12 (
    .D(multiplexer_12_out), .en(or_12_out), .clk(clk), .Q(register_12_q));  // open: clr
  or or_12 (or_12_out, Jen, decd11);
  Register #(.width(32)) register_13 (
    .D(multiplexer_13_out), .en(or_13_out), .clk(clk), .Q(register_13_q));  // open: clr
  or or_13 (or_13_out, Jen, decd12);
  Register #(.width(32)) register_14 (
    .D(multiplexer_14_out), .en(or_14_out), .clk(clk), .Q(register_14_q));  // open: clr
  or or_14 (or_14_out, Jen, decd13);
  Register #(.width(32)) register_15 (
    .D(multiplexer_15_out), .en(or_15_out), .clk(clk), .Q(register_15_q));  // open: clr
  or or_15 (or_15_out, Jen, decd14);
  Register #(.width(32)) register_16 (.D(multiplexer_16_out), .en(or_16_out), .clk(clk), .Q(Jout));  // open: clr
  or or_16 (or_16_out, Jen, decd15);
  Multiplexer #(.select(4), .width(32)) multiplexer_17 (
    .in0(register_1_q), .in1(register_2_q), .in2(register_3_q), .in3(register_4_q), .in4(register_5_q),
    .in5(register_6_q), .in6(register_7_q), .in7(register_8_q), .in8(register_9_q), .in9(register_10_q),
    .in10(register_11_q), .in11(register_12_q), .in12(register_13_q), .in13(register_14_q),
    .in14(register_15_q), .in15(Jout), .out(Dout), .sel(Addr));
  Decoder #(.select(4)) decoder_1 (
    .out0(decd0), .out1(decd1), .out2(decd2), .out3(decd3), .out4(decd4), .out5(decd5), .out6(decd6),
    .out7(decd7), .out8(decd8), .out9(decd9), .out10(decd10), .out11(decd11), .out12(decd12), .out13(decd13),
    .out14(decd14), .out15(decd15), .sel(Addr), .en(Wen));
endmodule

module memooory (
  input  [31:0] Jin,
  input  [31:0] Din,
  input  [8:0] Addr,
  input  clk,
  input  Wen,
  input  Jen,
  output [31:0] Jout,
  output [31:0] Dout
);

  wire EN0, EN1, EN2, EN3, EN4, EN5, EN6, EN7, EN8, EN9, EN10, EN11, EN12, EN13, EN14, EN15, EN16, EN17,
       EN18, EN19, EN20, EN21, EN22, EN23, EN24, EN25, EN26, EN27, EN28, EN29, EN30, EN31;
  wire [31:0] J3, J7, J11, J15, J19, J23, J27, OUT0, OUT1, OUT2, OUT3, OUT4, OUT5, OUT6, OUT7, OUT8, OUT9,
       OUT10, OUT11, OUT12, OUT13, OUT14, OUT15, OUT16, OUT17, OUT18, OUT19, OUT20, OUT21, OUT22, OUT23,
       OUT24, OUT25, OUT26, OUT27, OUT28, OUT29, OUT30, OUT31, Unit0_jout, Unit1_jout, Unit2_jout,
       Unit4_jout, Unit5_jout, Unit6_jout, Unit8_jout, Unit9_jout, Unit10_jout, Unit12_jout, Unit13_jout,
       Unit14_jout, Unit16_jout, Unit17_jout, Unit18_jout, Unit20_jout, Unit21_jout, Unit22_jout,
       Unit24_jout, Unit25_jout, Unit26_jout, Unit28_jout, Unit29_jout, Unit30_jout;

  RAM_16Word Unit0 (
    .Jin(Jin), .Din(Din), .Addr(Addr[3:0]), .clk(clk), .Wen(EN0), .Jen(Jen), .Jout(Unit0_jout), .Dout(OUT0));
  RAM_16Word Unit4 (
    .Jin(J3), .Din(Din), .Addr(Addr[3:0]), .clk(clk), .Wen(EN4), .Jen(Jen), .Jout(Unit4_jout), .Dout(OUT4));
  RAM_16Word Unit8 (
    .Jin(J7), .Din(Din), .Addr(Addr[3:0]), .clk(clk), .Wen(EN8), .Jen(Jen), .Jout(Unit8_jout), .Dout(OUT8));
  RAM_16Word Unit12 (
    .Jin(J11), .Din(Din), .Addr(Addr[3:0]), .clk(clk), .Wen(EN12), .Jen(Jen), .Jout(Unit12_jout), .Dout(OUT12));
  RAM_16Word Unit16 (
    .Jin(J15), .Din(Din), .Addr(Addr[3:0]), .clk(clk), .Wen(EN16), .Jen(Jen), .Jout(Unit16_jout), .Dout(OUT16));
  RAM_16Word Unit20 (
    .Jin(J19), .Din(Din), .Addr(Addr[3:0]), .clk(clk), .Wen(EN20), .Jen(Jen), .Jout(Unit20_jout), .Dout(OUT20));
  RAM_16Word Unit24 (
    .Jin(J23), .Din(Din), .Addr(Addr[3:0]), .clk(clk), .Wen(EN24), .Jen(Jen), .Jout(Unit24_jout), .Dout(OUT24));
  RAM_16Word Unit28 (
    .Jin(J27), .Din(Din), .Addr(Addr[3:0]), .clk(clk), .Wen(EN28), .Jen(Jen), .Jout(Unit28_jout), .Dout(OUT28));
  Decoder #(.select(5)) decoder_1 (
    .out0(EN0), .out1(EN1), .out2(EN2), .out3(EN3), .out4(EN4), .out5(EN5), .out6(EN6), .out7(EN7),
    .out8(EN8), .out9(EN9), .out10(EN10), .out11(EN11), .out12(EN12), .out13(EN13), .out14(EN14),
    .out15(EN15), .out16(EN16), .out17(EN17), .out18(EN18), .out19(EN19), .out20(EN20), .out21(EN21),
    .out22(EN22), .out23(EN23), .out24(EN24), .out25(EN25), .out26(EN26), .out27(EN27), .out28(EN28),
    .out29(EN29), .out30(EN30), .out31(EN31), .sel(Addr[8:4]), .en(Wen));
  RAM_16Word Unit1 (
    .Jin(Unit0_jout), .Din(Din), .Addr(Addr[3:0]), .clk(clk), .Wen(EN1), .Jen(Jen), .Jout(Unit1_jout),
    .Dout(OUT1));
  RAM_16Word Unit5 (
    .Jin(Unit4_jout), .Din(Din), .Addr(Addr[3:0]), .clk(clk), .Wen(EN5), .Jen(Jen), .Jout(Unit5_jout),
    .Dout(OUT5));
  RAM_16Word Unit9 (
    .Jin(Unit8_jout), .Din(Din), .Addr(Addr[3:0]), .clk(clk), .Wen(EN9), .Jen(Jen), .Jout(Unit9_jout),
    .Dout(OUT9));
  RAM_16Word Unit13 (
    .Jin(Unit12_jout), .Din(Din), .Addr(Addr[3:0]), .clk(clk), .Wen(EN13), .Jen(Jen), .Jout(Unit13_jout),
    .Dout(OUT13));
  RAM_16Word Unit17 (
    .Jin(Unit16_jout), .Din(Din), .Addr(Addr[3:0]), .clk(clk), .Wen(EN17), .Jen(Jen), .Jout(Unit17_jout),
    .Dout(OUT17));
  RAM_16Word Unit21 (
    .Jin(Unit20_jout), .Din(Din), .Addr(Addr[3:0]), .clk(clk), .Wen(EN21), .Jen(Jen), .Jout(Unit21_jout),
    .Dout(OUT21));
  RAM_16Word Unit25 (
    .Jin(Unit24_jout), .Din(Din), .Addr(Addr[3:0]), .clk(clk), .Wen(EN25), .Jen(Jen), .Jout(Unit25_jout),
    .Dout(OUT25));
  RAM_16Word Unit29 (
    .Jin(Unit28_jout), .Din(Din), .Addr(Addr[3:0]), .clk(clk), .Wen(EN29), .Jen(Jen), .Jout(Unit29_jout),
    .Dout(OUT29));
  RAM_16Word Unit2 (
    .Jin(Unit1_jout), .Din(Din), .Addr(Addr[3:0]), .clk(clk), .Wen(EN2), .Jen(Jen), .Jout(Unit2_jout),
    .Dout(OUT2));
  RAM_16Word Unit6 (
    .Jin(Unit5_jout), .Din(Din), .Addr(Addr[3:0]), .clk(clk), .Wen(EN6), .Jen(Jen), .Jout(Unit6_jout),
    .Dout(OUT6));
  RAM_16Word Unit10 (
    .Jin(Unit9_jout), .Din(Din), .Addr(Addr[3:0]), .clk(clk), .Wen(EN10), .Jen(Jen), .Jout(Unit10_jout),
    .Dout(OUT10));
  RAM_16Word Unit14 (
    .Jin(Unit13_jout), .Din(Din), .Addr(Addr[3:0]), .clk(clk), .Wen(EN14), .Jen(Jen), .Jout(Unit14_jout),
    .Dout(OUT14));
  RAM_16Word Unit18 (
    .Jin(Unit17_jout), .Din(Din), .Addr(Addr[3:0]), .clk(clk), .Wen(EN18), .Jen(Jen), .Jout(Unit18_jout),
    .Dout(OUT18));
  RAM_16Word Unit22 (
    .Jin(Unit21_jout), .Din(Din), .Addr(Addr[3:0]), .clk(clk), .Wen(EN22), .Jen(Jen), .Jout(Unit22_jout),
    .Dout(OUT22));
  RAM_16Word Unit26 (
    .Jin(Unit25_jout), .Din(Din), .Addr(Addr[3:0]), .clk(clk), .Wen(EN26), .Jen(Jen), .Jout(Unit26_jout),
    .Dout(OUT26));
  RAM_16Word Unit30 (
    .Jin(Unit29_jout), .Din(Din), .Addr(Addr[3:0]), .clk(clk), .Wen(EN30), .Jen(Jen), .Jout(Unit30_jout),
    .Dout(OUT30));
  RAM_16Word Unit3 (
    .Jin(Unit2_jout), .Din(Din), .Addr(Addr[3:0]), .clk(clk), .Wen(EN3), .Jen(Jen), .Jout(J3), .Dout(OUT3));
  RAM_16Word Unit7 (
    .Jin(Unit6_jout), .Din(Din), .Addr(Addr[3:0]), .clk(clk), .Wen(EN7), .Jen(Jen), .Jout(J7), .Dout(OUT7));
  RAM_16Word Unit11 (
    .Jin(Unit10_jout), .Din(Din), .Addr(Addr[3:0]), .clk(clk), .Wen(EN11), .Jen(Jen), .Jout(J11), .Dout(OUT11));
  RAM_16Word Unit15 (
    .Jin(Unit14_jout), .Din(Din), .Addr(Addr[3:0]), .clk(clk), .Wen(EN15), .Jen(Jen), .Jout(J15), .Dout(OUT15));
  RAM_16Word Unit19 (
    .Jin(Unit18_jout), .Din(Din), .Addr(Addr[3:0]), .clk(clk), .Wen(EN19), .Jen(Jen), .Jout(J19), .Dout(OUT19));
  RAM_16Word Unit23 (
    .Jin(Unit22_jout), .Din(Din), .Addr(Addr[3:0]), .clk(clk), .Wen(EN23), .Jen(Jen), .Jout(J23), .Dout(OUT23));
  RAM_16Word Unit27 (
    .Jin(Unit26_jout), .Din(Din), .Addr(Addr[3:0]), .clk(clk), .Wen(EN27), .Jen(Jen), .Jout(J27), .Dout(OUT27));
  RAM_16Word Unit31 (
    .Jin(Unit30_jout), .Din(Din), .Addr(Addr[3:0]), .clk(clk), .Wen(EN31), .Jen(Jen), .Jout(Jout),
    .Dout(OUT31));
  Multiplexer #(.select(5), .width(32)) multiplexer_1 (
    .in0(OUT0), .in1(OUT1), .in2(OUT2), .in3(OUT3), .in4(OUT4), .in5(OUT5), .in6(OUT6), .in7(OUT7),
    .in8(OUT8), .in9(OUT9), .in10(OUT10), .in11(OUT11), .in12(OUT12), .in13(OUT13), .in14(OUT14),
    .in15(OUT15), .in16(OUT16), .in17(OUT17), .in18(OUT18), .in19(OUT19), .in20(OUT20), .in21(OUT21),
    .in22(OUT22), .in23(OUT23), .in24(OUT24), .in25(OUT25), .in26(OUT26), .in27(OUT27), .in28(OUT28),
    .in29(OUT29), .in30(OUT30), .in31(OUT31), .out(Dout), .sel(Addr[8:4]));

  // Other names for the same wires on the sheet: InAddr[3:0] = Addr[3:0]; BlockAddr[4:0] = Addr[8:4]
endmodule

module regfillll (
  input  [4:0] Read0,
  input  [4:0] Read1,
  input  [4:0] Write,
  input  [31:0] Data,
  input  WriteReg,
  input  clk,
  input  rst,
  output [31:0] RegOut1,
  output [31:0] RegOut2,
  output [31:0] R0,
  output [31:0] R1,
  output [31:0] R2,
  output [31:0] R3,
  output [31:0] R4,
  output [31:0] R5,
  output [31:0] R6,
  output [31:0] R7,
  output [31:0] R8,
  output [31:0] R9,
  output [31:0] R10,
  output [31:0] R11,
  output [31:0] R12,
  output [31:0] R13,
  output [31:0] R14,
  output [31:0] R15,
  output [31:0] R16,
  output [31:0] R17,
  output [31:0] R18,
  output [31:0] R19,
  output [31:0] R20,
  output [31:0] R21,
  output [31:0] R22,
  output [31:0] R23,
  output [31:0] R24,
  output [31:0] R25,
  output [31:0] R26,
  output [31:0] R27,
  output [31:0] R28,
  output [31:0] R29,
  output [31:0] R30,
  output [31:0] R31
);

  wire and_1_out, and_2_out, and_3_out, and_4_out, and_5_out, and_6_out, and_7_out, and_8_out, and_9_out,
       and_10_out, and_11_out, and_12_out, and_13_out, and_14_out, and_15_out, and_16_out, and_17_out,
       and_18_out, and_19_out, and_20_out, and_21_out, and_22_out, and_23_out, and_24_out, and_25_out,
       and_26_out, and_27_out, and_28_out, and_29_out, and_30_out, and_31_out, w0, w1, w2, w3, w4, w5, w6,
       w7, w8, w9, w10, w11, w12, w13, w14, w15, w16, w17, w18, w19, w20, w21, w22, w23, w24, w25, w26, w27,
       w28, w29, w30, w31;

  Decoder #(.enable("false"), .select(5)) decoder_1 (
    .out0(w0), .out1(w1), .out2(w2), .out3(w3), .out4(w4), .out5(w5), .out6(w6), .out7(w7), .out8(w8),
    .out9(w9), .out10(w10), .out11(w11), .out12(w12), .out13(w13), .out14(w14), .out15(w15), .out16(w16),
    .out17(w17), .out18(w18), .out19(w19), .out20(w20), .out21(w21), .out22(w22), .out23(w23), .out24(w24),
    .out25(w25), .out26(w26), .out27(w27), .out28(w28), .out29(w29), .out30(w30), .out31(w31), .sel(Write));
  and and_1 (and_1_out, WriteReg, w4);
  and and_2 (and_2_out, WriteReg, w8);
  and and_3 (and_3_out, WriteReg, w12);
  and and_4 (and_4_out, WriteReg, w16);
  and and_5 (and_5_out, WriteReg, w20);
  and and_6 (and_6_out, WriteReg, w24);
  and and_7 (and_7_out, WriteReg, w28);
  Register #(.width(32)) register_1 (.D(Data), .en(and_1_out), .clk(clk), .Q(R4), .clr(rst));
  Register #(.width(32)) register_2 (.D(Data), .en(and_2_out), .clk(clk), .Q(R8), .clr(rst));
  Register #(.width(32)) register_3 (.D(Data), .en(and_3_out), .clk(clk), .Q(R12), .clr(rst));
  Register #(.width(32)) register_4 (.D(Data), .en(and_4_out), .clk(clk), .Q(R16), .clr(rst));
  Register #(.width(32)) register_5 (.D(Data), .en(and_5_out), .clk(clk), .Q(R20), .clr(rst));
  Register #(.width(32)) register_6 (.D(Data), .en(and_6_out), .clk(clk), .Q(R24), .clr(rst));
  Register #(.width(32)) register_7 (.D(Data), .en(and_7_out), .clk(clk), .Q(R28), .clr(rst));
  and and_8 (and_8_out, WriteReg, w1);
  and and_9 (and_9_out, WriteReg, w5);
  and and_10 (and_10_out, WriteReg, w9);
  and and_11 (and_11_out, WriteReg, w13);
  and and_12 (and_12_out, WriteReg, w17);
  and and_13 (and_13_out, WriteReg, w21);
  and and_14 (and_14_out, WriteReg, w25);
  and and_15 (and_15_out, WriteReg, w29);
  Register #(.width(32)) register_8 (.D(Data), .en(and_8_out), .clk(clk), .Q(R1), .clr(rst));
  Register #(.width(32)) register_9 (.D(Data), .en(and_9_out), .clk(clk), .Q(R5), .clr(rst));
  Register #(.width(32)) register_10 (.D(Data), .en(and_10_out), .clk(clk), .Q(R9), .clr(rst));
  Register #(.width(32)) register_11 (.D(Data), .en(and_11_out), .clk(clk), .Q(R13), .clr(rst));
  Register #(.width(32)) register_12 (.D(Data), .en(and_12_out), .clk(clk), .Q(R17), .clr(rst));
  Register #(.width(32)) register_13 (.D(Data), .en(and_13_out), .clk(clk), .Q(R21), .clr(rst));
  Register #(.width(32)) register_14 (.D(Data), .en(and_14_out), .clk(clk), .Q(R25), .clr(rst));
  Register #(.width(32)) register_15 (.D(Data), .en(and_15_out), .clk(clk), .Q(R29), .clr(rst));
  and and_16 (and_16_out, WriteReg, w6);
  and and_17 (and_17_out, WriteReg, w22);
  and and_18 (and_18_out, WriteReg, w2);
  and and_19 (and_19_out, WriteReg, w10);
  and and_20 (and_20_out, WriteReg, w14);
  and and_21 (and_21_out, WriteReg, w18);
  and and_22 (and_22_out, WriteReg, w26);
  and and_23 (and_23_out, WriteReg, w30);
  Register #(.width(32)) register_16 (.D(Data), .en(and_18_out), .clk(clk), .Q(R2), .clr(rst));
  Register #(.width(32)) register_17 (.D(Data), .en(and_16_out), .clk(clk), .Q(R6), .clr(rst));
  Register #(.width(32)) register_18 (.D(Data), .en(and_19_out), .clk(clk), .Q(R10), .clr(rst));
  Register #(.width(32)) register_19 (.D(Data), .en(and_20_out), .clk(clk), .Q(R14), .clr(rst));
  Register #(.width(32)) register_20 (.D(Data), .en(and_21_out), .clk(clk), .Q(R18), .clr(rst));
  Register #(.width(32)) register_21 (.D(Data), .en(and_17_out), .clk(clk), .Q(R22), .clr(rst));
  Register #(.width(32)) register_22 (.D(Data), .en(and_22_out), .clk(clk), .Q(R26), .clr(rst));
  Register #(.width(32)) register_23 (.D(Data), .en(and_23_out), .clk(clk), .Q(R30), .clr(rst));
  and and_24 (and_24_out, WriteReg, w7);
  and and_25 (and_25_out, WriteReg, w23);
  and and_26 (and_26_out, WriteReg, w3);
  and and_27 (and_27_out, WriteReg, w11);
  and and_28 (and_28_out, WriteReg, w15);
  and and_29 (and_29_out, WriteReg, w19);
  and and_30 (and_30_out, WriteReg, w27);
  and and_31 (and_31_out, WriteReg, w31);
  Register #(.width(32)) register_24 (.D(Data), .en(and_26_out), .clk(clk), .Q(R3), .clr(rst));
  Register #(.width(32)) register_25 (.D(Data), .en(and_24_out), .clk(clk), .Q(R7), .clr(rst));
  Register #(.width(32)) register_26 (.D(Data), .en(and_27_out), .clk(clk), .Q(R11), .clr(rst));
  Register #(.width(32)) register_27 (.D(Data), .en(and_28_out), .clk(clk), .Q(R15), .clr(rst));
  Register #(.width(32)) register_28 (.D(Data), .en(and_29_out), .clk(clk), .Q(R19), .clr(rst));
  Register #(.width(32)) register_29 (.D(Data), .en(and_25_out), .clk(clk), .Q(R23), .clr(rst));
  Register #(.width(32)) register_30 (.D(Data), .en(and_30_out), .clk(clk), .Q(R27), .clr(rst));
  Register #(.width(32)) register_31 (.D(Data), .en(and_31_out), .clk(clk), .Q(R31), .clr(rst));
  Multiplexer #(.select(5), .width(32)) multiplexer_1 (
    .in0({32{1'b0}}), .in1(R1), .in2(R2), .in3(R3), .in4(R4), .in5(R5), .in6(R6), .in7(R7), .in8(R8),
    .in9(R9), .in10(R10), .in11(R11), .in12(R12), .in13(R13), .in14(R14), .in15(R15), .in16(R16), .in17(R17),
    .in18(R18), .in19(R19), .in20(R20), .in21(R21), .in22(R22), .in23(R23), .in24(R24), .in25(R25),
    .in26(R26), .in27(R27), .in28(R28), .in29(R29), .in30(R30), .in31(R31), .out(RegOut1), .sel(Read0));
  Multiplexer #(.select(5), .width(32)) multiplexer_2 (
    .in0({32{1'b0}}), .in1(R1), .in2(R2), .in3(R3), .in4(R4), .in5(R5), .in6(R6), .in7(R7), .in8(R8),
    .in9(R9), .in10(R10), .in11(R11), .in12(R12), .in13(R13), .in14(R14), .in15(R15), .in16(R16), .in17(R17),
    .in18(R18), .in19(R19), .in20(R20), .in21(R21), .in22(R22), .in23(R23), .in24(R24), .in25(R25),
    .in26(R26), .in27(R27), .in28(R28), .in29(R29), .in30(R30), .in31(R31), .out(RegOut2), .sel(Read1));

  assign R0 = {32{1'b0}};

  // Other names for the same wires on the sheet: clockk = clk; d1[31:0] = R1; d2[31:0] = R2; d3[31:0] = R3;
  //   d4[31:0] = R4; d5[31:0] = R5; d6[31:0] = R6; d7[31:0] = R7; d8[31:0] = R8; d9[31:0] = R9; d10[31:0] = R10;
  //   d11[31:0] = R11; d12[31:0] = R12; d13[31:0] = R13; d14[31:0] = R14; d15[31:0] = R15; d16[31:0] = R16;
  //   d17[31:0] = R17; d18[31:0] = R18; d19[31:0] = R19; d20[31:0] = R20; d21[31:0] = R21; d22[31:0] = R22;
  //   d23[31:0] = R23; d24[31:0] = R24; d25[31:0] = R25; d26[31:0] = R26; d27[31:0] = R27; d28[31:0] = R28;
  //   d29[31:0] = R29; d30[31:0] = R30; d31[31:0] = R31; dataaaa[31:0] = Data; out1[31:0] = RegOut1;
  //   out2[31:0] = RegOut2; restttttttt = rst; wre = WriteReg
endmodule

module aluuuuuu (
  input  [31:0] b,
  input  output_inc,
  input  [31:0] a,
  input  [3:0] aluop,
  input  output_inverted,
  input  clkk,
  input  rsstt,
  input  startdivvand,
  input  isdivv,
  output [31:0] res_low,
  output [31:0] res_high,
  output done
);

  wire [31:0] asghar_res_hi, asghar_res_lo;

  operation asghar (
    .b(b), .a(a), .opcode(aluop), .clkk(clkk), .rstt(rsstt), .divandd(startdivvand), .isdivv(isdivv),
    .res_lo(asghar_res_lo), .res_hi(asghar_res_hi), .done(done));
  make_result mamad (
    .output_inc(output_inc), .lo_in(asghar_res_lo), .output_inverted(output_inverted), .hi_in(asghar_res_hi),
    .res_lo(res_low), .res_hi(res_high));
endmodule

module operation (
  input  [31:0] b,
  input  [31:0] a,
  input  [3:0] opcode,
  input  clkk,
  input  rstt,
  input  divandd,
  input  isdivv,
  output [31:0] res_lo,
  output [31:0] res_hi,
  output done
);

  wire and_1_out, diiiiv_done, startttdiv_strt;
  wire [31:0] addeman_res_hi, addeman_res_lo, andeman_res_hi, andeman_res_lo, cloman_res_hi, cloman_res_lo,
       clzman_res_hi, clzman_res_lo, diiiiv_quotient, diiiiv_remainder, oreman_res_hi, oreman_res_lo,
       rotrman_res_hi, rotrman_res_lo, sllleman_res_hi, sllleman_res_lo, slt_1_res_hi, slt_1_res_lo,
       sraman_res_hi, sraman_res_lo, srlman_res_hi, srlman_res_lo, subeman_res_hi, subeman_res_lo,
       xoreman_res_hi, xoreman_res_lo;

  start startttdiv (.rst(rstt), .clk(clkk), .isdivv(isdivv), .strt(startttdiv_strt));
  and and_1 (and_1_out, startttdiv_strt, divandd);
  addddd addeman (.a(a), .b(b), .res_lo(addeman_res_lo), .res_hi(addeman_res_hi));
  subbbbb subeman (.a(a), .b(b), .res_lo(subeman_res_lo), .res_hi(subeman_res_hi));
  div diiiiv (
    .dividend(a), .start(and_1_out), .clk(clkk), .rst(rstt), .divisor(b), .remainder(diiiiv_remainder),
    .quotient(diiiiv_quotient), .done(diiiiv_done));
  aaand andeman (.a(a), .b(b), .res_lo(andeman_res_lo), .res_hi(andeman_res_hi));
  ooor oreman (.a(a), .b(b), .res_lo(oreman_res_lo), .res_hi(oreman_res_hi));
  xoooor xoreman (.a(a), .b(b), .res_lo(xoreman_res_lo), .res_hi(xoreman_res_hi));
  clooo cloman (.a(a), .res_lo(cloman_res_lo), .res_hi(cloman_res_hi));
  clz clzman (.a(a), .res_lo(clzman_res_lo), .res_hi(clzman_res_hi));
  sllll sllleman (.a(a), .b(b), .res_lo(sllleman_res_lo), .res_hi(sllleman_res_hi));
  srllll srlman (.a(a), .b(b), .res_lo(srlman_res_lo), .res_hi(srlman_res_hi));
  sraaaa sraman (.a(a), .b(b), .res_lo(sraman_res_lo), .res_hi(sraman_res_hi));
  rotrrrr rotrman (.a(a), .b(b), .res_lo(rotrman_res_lo), .res_hi(rotrman_res_hi));
  slt slt_1 (.a(a), .b(b), .res_lo(slt_1_res_lo), .res_hi(slt_1_res_hi));
  and and_2 (done, diiiiv_done, isdivv);
  Multiplexer #(.select(4), .width(32)) multiplexer_1 (
    .in0(addeman_res_hi), .in1(subeman_res_hi), .in3(diiiiv_remainder), .in4(andeman_res_hi),
    .in5(oreman_res_hi), .in6(xoreman_res_hi), .in7(cloman_res_hi), .in8(clzman_res_hi),
    .in9(sllleman_res_hi), .in10(srlman_res_hi), .in11(sraman_res_hi), .in12(rotrman_res_hi),
    .in13(slt_1_res_hi), .out(res_hi), .sel(opcode));  // open: in2, in14, in15
  Multiplexer #(.select(4), .width(32)) multiplexer_2 (
    .in0(addeman_res_lo), .in1(subeman_res_lo), .in3(diiiiv_quotient), .in4(andeman_res_lo),
    .in5(oreman_res_lo), .in6(xoreman_res_lo), .in7(cloman_res_lo), .in8(clzman_res_lo),
    .in9(sllleman_res_lo), .in10(srlman_res_lo), .in11(sraman_res_lo), .in12(rotrman_res_lo),
    .in13(slt_1_res_lo), .out(res_lo), .sel(opcode));  // open: in2, in14, in15
endmodule

module addddd (
  input  [31:0] a,
  input  [31:0] b,
  output [31:0] res_lo,
  output [31:0] res_hi
);

  Adder #(.width(32)) adder_1 (.a(a), .b(b), .out(res_lo), .cin(1'b0), .cout(res_hi[0]));

  assign res_hi[31:1] = {31{1'b0}};
endmodule

module subbbbb (
  input  [31:0] a,
  input  [31:0] b,
  output [31:0] res_lo,
  output [31:0] res_hi
);

  wire comparator_1_lt;
  wire [31:0] not_1_out;

  assign not_1_out = ~b;  // NOT_Gate not_1, 32 bits wide
  Comparator #(.mode("unsigned"), .width(32)) comparator_1 (.a(a), .b(b), .lt(comparator_1_lt));  // open: gt, eq
  Adder #(.width(32)) adder_1 (.a(a), .b(not_1_out), .out(res_lo), .cin(1'b1));  // open: cout
  assign res_hi = {{31{comparator_1_lt}}, comparator_1_lt};  // Bit_Extender bit_extender_1
endmodule

module start (
  input  rst,
  input  clk,
  input  isdivv,
  output strt
);

  wire d_ff_1_q, not_1_out;

  D_Flip_Flop d_ff_1 (.D(isdivv), .clk(clk), .Q(d_ff_1_q), .reset(rst));  // open: Qn, preset
  not not_1 (not_1_out, d_ff_1_q);
  and and_1 (strt, isdivv, not_1_out);
endmodule

module aaand (
  input  [31:0] a,
  input  [31:0] b,
  output [31:0] res_lo,
  output [31:0] res_hi
);

  assign res_lo = a & b;  // AND_Gate and_1, 32 bits wide

  assign res_hi = {32{1'b0}};
endmodule

module ooor (
  input  [31:0] a,
  input  [31:0] b,
  output [31:0] res_lo,
  output [31:0] res_hi
);

  assign res_lo = a | b;  // OR_Gate or_1, 32 bits wide

  assign res_hi = {32{1'b0}};
endmodule

module xoooor (
  input  [31:0] a,
  input  [31:0] b,
  output [31:0] res_lo,
  output [31:0] res_hi
);

  assign res_lo = a ^ b;  // XOR_Gate xor_1, 32 bits wide

  assign res_hi = {32{1'b0}};
endmodule

module make_result (
  input  output_inc,
  input  [31:0] lo_in,
  input  output_inverted,
  input  [31:0] hi_in,
  output [31:0] res_lo,
  output [31:0] res_hi
);

  wire adder_2_cout;
  wire [31:0] multiplexer_1_out, multiplexer_2_out, not_1_out, not_2_out;

  assign not_1_out = ~lo_in;  // NOT_Gate not_1, 32 bits wide
  Multiplexer #(.width(32)) multiplexer_1 (
    .in0(hi_in), .in1(not_2_out), .out(multiplexer_1_out), .sel(output_inverted));
  assign not_2_out = ~hi_in;  // NOT_Gate not_2, 32 bits wide
  Multiplexer #(.width(32)) multiplexer_2 (
    .in0(lo_in), .in1(not_1_out), .out(multiplexer_2_out), .sel(output_inverted));
  Adder #(.width(32)) adder_1 (.a(multiplexer_1_out), .b({32{1'b0}}), .out(res_hi), .cin(adder_2_cout));  // open: cout
  Adder #(.width(32)) adder_2 (
    .a(multiplexer_2_out), .b({32{1'b0}}), .out(res_lo), .cin(output_inc), .cout(adder_2_cout));
endmodule

module clooo (
  input  [31:0] a,
  output [31:0] res_lo,
  output [31:0] res_hi
);

  wire comparator_1_eq;
  wire [0:0] multiplexer_5_out;
  wire [3:0] multiplexer_4_out;
  wire [4:0] or_4_out;
  wire [7:0] multiplexer_3_out;
  wire [15:0] multiplexer_1_out;
  wire [31:0] bit_extender_1_out, not_1_out, subtractor_1_out;

  assign not_1_out = ~a;  // NOT_Gate not_1, 32 bits wide
  or or_1 (or_4_out[4], not_1_out[16], not_1_out[17], not_1_out[18], not_1_out[19], not_1_out[20], not_1_out[21], not_1_out[22], not_1_out[23], not_1_out[25], not_1_out[26], not_1_out[27], not_1_out[28], not_1_out[29], not_1_out[30], not_1_out[31], not_1_out[24]);
  Comparator #(.width(32)) comparator_1 (.a(not_1_out), .b({32{1'b0}}), .eq(comparator_1_eq));  // open: gt, lt
  Multiplexer #(.width(16)) multiplexer_1 (
    .in0(not_1_out[15:0]), .in1(not_1_out[31:16]), .out(multiplexer_1_out), .sel(or_4_out[4]));
  or or_2 (or_4_out[3], multiplexer_1_out[8], multiplexer_1_out[9], multiplexer_1_out[10], multiplexer_1_out[11], multiplexer_1_out[13], multiplexer_1_out[14], multiplexer_1_out[15], multiplexer_1_out[12]);
  Multiplexer #(.width(32)) multiplexer_2 (.in0(subtractor_1_out), .in1(32'h20), .out(res_lo), .sel(comparator_1_eq));
  assign bit_extender_1_out = {{27{1'b0}}, or_4_out};  // Bit_Extender bit_extender_1
  Multiplexer #(.width(8)) multiplexer_3 (
    .in0(multiplexer_1_out[7:0]), .in1(multiplexer_1_out[15:8]), .out(multiplexer_3_out), .sel(or_4_out[3]));
  Subtractor #(.width(32)) subtractor_1 (
    .a(32'h1f), .b(bit_extender_1_out), .out(subtractor_1_out), .bin(1'b0));  // open: bout
  or or_3 (or_4_out[2], multiplexer_3_out[4], multiplexer_3_out[5], multiplexer_3_out[7], multiplexer_3_out[6]);
  Multiplexer #(.width(4)) multiplexer_4 (
    .in0(multiplexer_3_out[3:0]), .in1(multiplexer_3_out[7:4]), .out(multiplexer_4_out), .sel(or_4_out[2]));
  or or_4 (or_4_out[1], multiplexer_4_out[2], multiplexer_4_out[3]);
  Multiplexer #(.width(2)) multiplexer_5 (
    .in0(multiplexer_4_out[1:0]), .in1(multiplexer_4_out[3:2]), .out({or_4_out[0], multiplexer_5_out[0]}),
    .sel(or_4_out[1]));

  assign res_hi = {32{1'b0}};
endmodule

module clz (
  input  [31:0] a,
  output [31:0] res_lo,
  output [31:0] res_hi
);

  wire comparator_1_eq;
  wire [0:0] multiplexer_5_out;
  wire [3:0] multiplexer_4_out;
  wire [4:0] or_4_out;
  wire [7:0] multiplexer_3_out;
  wire [15:0] multiplexer_1_out;
  wire [31:0] bit_extender_1_out, subtractor_1_out;

  or or_1 (or_4_out[4], a[16], a[17], a[18], a[19], a[20], a[21], a[22], a[23], a[25], a[26], a[27], a[28], a[29], a[30], a[31], a[24]);
  Comparator #(.width(32)) comparator_1 (.a(a), .b({32{1'b0}}), .eq(comparator_1_eq));  // open: gt, lt
  Multiplexer #(.width(16)) multiplexer_1 (.in0(a[15:0]), .in1(a[31:16]), .out(multiplexer_1_out), .sel(or_4_out[4]));
  or or_2 (or_4_out[3], multiplexer_1_out[8], multiplexer_1_out[9], multiplexer_1_out[10], multiplexer_1_out[11], multiplexer_1_out[13], multiplexer_1_out[14], multiplexer_1_out[15], multiplexer_1_out[12]);
  Multiplexer #(.width(32)) multiplexer_2 (.in0(subtractor_1_out), .in1(32'h20), .out(res_lo), .sel(comparator_1_eq));
  assign bit_extender_1_out = {{27{1'b0}}, or_4_out};  // Bit_Extender bit_extender_1
  Multiplexer #(.width(8)) multiplexer_3 (
    .in0(multiplexer_1_out[7:0]), .in1(multiplexer_1_out[15:8]), .out(multiplexer_3_out), .sel(or_4_out[3]));
  Subtractor #(.width(32)) subtractor_1 (
    .a(32'h1f), .b(bit_extender_1_out), .out(subtractor_1_out), .bin(1'b0));  // open: bout
  or or_3 (or_4_out[2], multiplexer_3_out[4], multiplexer_3_out[5], multiplexer_3_out[7], multiplexer_3_out[6]);
  Multiplexer #(.width(4)) multiplexer_4 (
    .in0(multiplexer_3_out[3:0]), .in1(multiplexer_3_out[7:4]), .out(multiplexer_4_out), .sel(or_4_out[2]));
  or or_4 (or_4_out[1], multiplexer_4_out[2], multiplexer_4_out[3]);
  Multiplexer #(.width(2)) multiplexer_5 (
    .in0(multiplexer_4_out[1:0]), .in1(multiplexer_4_out[3:2]), .out({or_4_out[0], multiplexer_5_out[0]}),
    .sel(or_4_out[1]));

  assign res_hi = {32{1'b0}};
endmodule

module sllll (
  input  [31:0] a,
  input  [31:0] b,
  output [31:0] res_lo,
  output [31:0] res_hi
);

  wire [15:0] multiplexer_4_out;
  wire [47:0] multiplexer_4_out_2;
  wire [63:0] bit_extender_1_out, multiplexer_1_out, multiplexer_2_out, multiplexer_3_out;

  assign bit_extender_1_out = {{32{1'b0}}, a};  // Bit_Extender bit_extender_1
  Multiplexer #(.width(64)) multiplexer_1 (
    .in0(bit_extender_1_out), .in1({bit_extender_1_out[62:0], 1'b0}), .out(multiplexer_1_out), .sel(b[0]));
  Multiplexer #(.width(64)) multiplexer_2 (
    .in0(multiplexer_1_out), .in1({multiplexer_1_out[61:0], 2'b00}), .out(multiplexer_2_out), .sel(b[1]));
  Multiplexer #(.width(64)) multiplexer_3 (
    .in0(multiplexer_2_out), .in1({multiplexer_2_out[59:0], 4'b0000}), .out(multiplexer_3_out), .sel(b[2]));
  Multiplexer #(.width(64)) multiplexer_4 (
    .in0(multiplexer_3_out), .in1({multiplexer_3_out[55:0], {8{1'b0}}}),
    .out({multiplexer_4_out, multiplexer_4_out_2}), .sel(b[3]));
  Multiplexer #(.width(64)) multiplexer_5 (
    .in0({multiplexer_4_out, multiplexer_4_out_2}), .in1({multiplexer_4_out_2, {16{1'b0}}}),
    .out({res_hi, res_lo}), .sel(b[4]));
endmodule

module srllll (
  input  [31:0] a,
  input  [31:0] b,
  output [31:0] res_lo,
  output [31:0] res_hi
);

  wire [15:0] multiplexer_4_out, multiplexer_4_out_2;
  wire [31:0] multiplexer_1_out, multiplexer_2_out, multiplexer_3_out;

  Multiplexer #(.width(32)) multiplexer_1 (.in0(a), .in1({1'b0, a[31:1]}), .out(multiplexer_1_out), .sel(b[0]));
  Multiplexer #(.width(32)) multiplexer_2 (
    .in0(multiplexer_1_out), .in1({2'b00, multiplexer_1_out[31:2]}), .out(multiplexer_2_out), .sel(b[1]));
  Multiplexer #(.width(32)) multiplexer_3 (
    .in0(multiplexer_2_out), .in1({4'b0000, multiplexer_2_out[31:4]}), .out(multiplexer_3_out), .sel(b[2]));
  Multiplexer #(.width(32)) multiplexer_4 (
    .in0(multiplexer_3_out), .in1({{8{1'b0}}, multiplexer_3_out[31:8]}),
    .out({multiplexer_4_out_2, multiplexer_4_out}), .sel(b[3]));
  Multiplexer #(.width(32)) multiplexer_5 (
    .in0({multiplexer_4_out_2, multiplexer_4_out}), .in1({{16{1'b0}}, multiplexer_4_out_2}), .out(res_lo),
    .sel(b[4]));

  assign res_hi = {32{1'b0}};
endmodule

module sraaaa (
  input  [31:0] a,
  input  [31:0] b,
  output [31:0] res_lo,
  output [31:0] res_hi
);

  wire [1:0] bit_extender_1_out;
  wire [3:0] bit_extender_2_out;
  wire [7:0] bit_extender_3_out;
  wire [31:0] multiplexer_1_out, multiplexer_2_out, multiplexer_3_out, multiplexer_4_out;
  wire [31:16] bit_extender_4_out;

  assign bit_extender_1_out = {{1{a[31]}}, a[31]};  // Bit_Extender bit_extender_1
  Multiplexer #(.width(32)) multiplexer_1 (.in0(a), .in1({{2{a[31]}}, a[30:1]}), .out(multiplexer_1_out), .sel(b[0]));
  Multiplexer #(.width(32)) multiplexer_2 (
    .in0(multiplexer_1_out), .in1({bit_extender_1_out, multiplexer_1_out[31:2]}), .out(multiplexer_2_out),
    .sel(b[1]));
  assign bit_extender_2_out = {{2{bit_extender_1_out[1]}}, bit_extender_1_out};  // Bit_Extender bit_extender_2
  Multiplexer #(.width(32)) multiplexer_3 (
    .in0(multiplexer_2_out), .in1({bit_extender_2_out, multiplexer_2_out[31:4]}), .out(multiplexer_3_out),
    .sel(b[2]));
  assign bit_extender_3_out = {{4{bit_extender_2_out[3]}}, bit_extender_2_out};  // Bit_Extender bit_extender_3
  assign bit_extender_4_out = {{8{bit_extender_3_out[7]}}, bit_extender_3_out};  // Bit_Extender bit_extender_4
  Multiplexer #(.width(32)) multiplexer_4 (
    .in0(multiplexer_3_out), .in1({bit_extender_3_out, multiplexer_3_out[31:8]}), .out(multiplexer_4_out),
    .sel(b[3]));
  Multiplexer #(.width(32)) multiplexer_5 (
    .in0(multiplexer_4_out), .in1({bit_extender_4_out, multiplexer_4_out[31:16]}), .out(res_lo), .sel(b[4]));
  assign res_hi = {{31{res_lo[31]}}, res_lo[31]};  // Bit_Extender bit_extender_5
endmodule

module rotrrrr (
  input  [31:0] a,
  input  [31:0] b,
  output [31:0] res_lo,
  output [31:0] res_hi
);

  wire [31:0] multiplexer_1_out, multiplexer_2_out, multiplexer_3_out, multiplexer_4_out;

  Multiplexer #(.width(32)) multiplexer_1 (.in0(a), .in1({a[0], a[31:1]}), .out(multiplexer_1_out), .sel(b[0]));
  Multiplexer #(.width(32)) multiplexer_2 (
    .in0(multiplexer_1_out), .in1({multiplexer_1_out[1:0], multiplexer_1_out[31:2]}),
    .out(multiplexer_2_out), .sel(b[1]));
  Multiplexer #(.width(32)) multiplexer_3 (
    .in0(multiplexer_2_out), .in1({multiplexer_2_out[3:0], multiplexer_2_out[31:4]}),
    .out(multiplexer_3_out), .sel(b[2]));
  Multiplexer #(.width(32)) multiplexer_4 (
    .in0(multiplexer_3_out), .in1({multiplexer_3_out[7:0], multiplexer_3_out[31:8]}),
    .out(multiplexer_4_out), .sel(b[3]));
  Multiplexer #(.width(32)) multiplexer_5 (
    .in0(multiplexer_4_out), .in1({multiplexer_4_out[15:0], multiplexer_4_out[31:16]}), .out(res_lo),
    .sel(b[4]));

  assign res_hi = {32{1'b0}};
endmodule

module opcodesaaz (
  input  [1:0] ALUOp,
  input  [5:0] functt,
  output [3:0] aloup
);

  wire [3:0] Artithmetic, R_type, Shift, undriven;

  Multiplexer #(.select(3), .width(4)) multiplexer_1 (
    .in0(Shift), .in1(4'b0000), .in2(undriven), .in3(4'b0011), .in4(Artithmetic), .out(R_type),
    .sel(functt[5:3]));  // open: in5, in6, in7
  Multiplexer #(.select(3), .width(4)) multiplexer_2 (
    .in0(4'b0000), .in2(4'b0001), .in4(4'b0100), .in5(4'b0101), .in6(4'b0110), .out(Artithmetic),
    .sel(functt[2:0]));  // open: in1, in3, in7
  Multiplexer #(.select(3), .width(4)) multiplexer_3 (
    .in0(4'b1001), .in4(4'b1001), .in6(4'b1010), .in7(4'b1011), .out(Shift), .sel(functt[2:0]));  // open: in1, in2, in3, in5
  Multiplexer #(.select(2), .width(4)) multiplexer_4 (
    .in0(4'b0000), .in1(4'b0001), .in2(R_type), .in3(4'b1101), .out(aloup), .sel(ALUOp));
endmodule

module slt (
  input  [31:0] a,
  input  [31:0] b,
  output [31:0] res_lo,
  output [31:0] res_hi
);

  wire comparator_1_lt;

  Comparator #(.width(32)) comparator_1 (.a(a), .b(b), .lt(comparator_1_lt));  // open: gt, eq
  assign res_lo = {{31{1'b0}}, comparator_1_lt};  // Bit_Extender bit_extender_1

  assign res_hi = {32{1'b0}};
endmodule

module div (
  input  [31:0] dividend,
  input  start,
  input  clk,
  input  rst,
  input  [31:0] divisor,
  output [31:0] remainder,
  output [31:0] quotient,
  output done
);

  wire and_1_out, and_2_out, comparator_1_eq, comparator_2_lt, d_ff_1_q, multiplexer_6_out, not_1_out,
       not_2_out, or_1_out, or_2_out, or_3_out, S1_q, S2_qn;
  wire [7:0] Counter_q, multiplexer_5_out, subtractor_2_out;
  wire [31:0] A_q, adder_1_out, adder_2_out, multiplexer_1_out, multiplexer_2_out, multiplexer_3_out,
       multiplexer_4_out, shifter_1_out, shifter_2_out, shifter_3_out, subtractor_1_out;

  D_Flip_Flop d_ff_1 (.D(start), .clk(clk), .Q(d_ff_1_q));  // open: Qn, preset, reset
  or or_1 (or_1_out, start, d_ff_1_q);
  Multiplexer #(.width(32)) multiplexer_1 (
    .in0(adder_1_out), .in1(subtractor_1_out), .out(multiplexer_1_out), .sel(not_1_out));
  Register #(.width(32)) A (.D(multiplexer_2_out), .en(S2_qn), .clk(clk), .Q(A_q), .clr(rst));
  Multiplexer #(.width(32)) multiplexer_2 (
    .in0(shifter_1_out), .in1(dividend), .out(multiplexer_2_out), .sel(or_1_out));
  Register #(.width(32)) R (.D(multiplexer_3_out), .en(S2_qn), .clk(clk), .Q(remainder), .clr(rst));
  Multiplexer #(.width(32)) multiplexer_3 (
    .in0(multiplexer_1_out), .in1({32{1'b0}}), .out(multiplexer_3_out), .sel(or_1_out));
  Register #(.width(32)) Q (.D(multiplexer_4_out), .en(S2_qn), .clk(clk), .Q(quotient), .clr(rst));
  Multiplexer #(.width(32)) multiplexer_4 (
    .in0(adder_2_out), .in1({32{1'b0}}), .out(multiplexer_4_out), .sel(or_1_out));
  Register Counter (.D(multiplexer_5_out), .en(S2_qn), .clk(clk), .Q(Counter_q), .clr(rst));
  Multiplexer #(.width(8)) multiplexer_5 (.in0(subtractor_2_out), .in1(8'h1f), .out(multiplexer_5_out), .sel(or_1_out));
  Shifter #(.width(32)) shifter_1 (.in(A_q), .\dist (5'b00001), .out(shifter_1_out));
  Shifter #(.width(32)) shifter_2 (.in(remainder), .\dist (5'b00001), .out(shifter_2_out));
  Shifter #(.width(32)) shifter_3 (.in(quotient), .\dist (5'b00001), .out(shifter_3_out));
  Adder #(.width(32)) adder_1 (.a(shifter_2_out), .b({32{1'b0}}), .out(adder_1_out), .cin(A_q[31]));  // open: cout
  Adder #(.width(32)) adder_2 (.a(shifter_3_out), .b({32{1'b0}}), .out(adder_2_out), .cin(not_1_out));  // open: cout
  Comparator comparator_1 (.a(Counter_q), .b({8{1'b0}}), .eq(comparator_1_eq));  // open: gt, lt
  Subtractor #(.width(32)) subtractor_1 (
    .a(adder_1_out), .b(divisor), .out(subtractor_1_out), .bin(1'b0));  // open: bout
  Comparator #(.mode("unsigned"), .width(32)) comparator_2 (
    .a(adder_1_out), .b(divisor), .lt(comparator_2_lt));  // open: gt, eq
  not not_1 (not_1_out, comparator_2_lt);
  Subtractor subtractor_2 (.a(Counter_q), .b(8'h1), .out(subtractor_2_out), .bin(1'b0));  // open: bout
  and and_1 (and_1_out, S1_q, not_2_out);
  not not_2 (not_2_out, comparator_1_eq);
  and and_2 (and_2_out, S1_q, comparator_1_eq);
  D_Flip_Flop S1 (.D(or_2_out), .clk(clk), .Q(S1_q), .reset(rst));  // open: Qn, preset
  or or_2 (or_2_out, or_1_out, and_1_out);
  or or_3 (or_3_out, done, and_2_out);
  D_Flip_Flop S2 (.D(multiplexer_6_out), .clk(clk), .Q(done), .Qn(S2_qn), .reset(rst));  // open: preset
  Multiplexer multiplexer_6 (.in0(or_3_out), .in1(1'b0), .out(multiplexer_6_out), .sel(or_1_out));
endmodule

module startt (
  input  rst,
  input  clk,
  input  [31:0] a,
  input  [31:0] b,
  output strt,
  output donekosh
);

  wire comparator_1_eq, comparator_2_eq, comparator_3_eq, d_ff_1_q, d_ff_2_q, d_ff_3_q, not_1_out, not_2_out,
       not_3_out, or_1_out;
  wire [31:0] register_1_q, register_2_q;

  D_Flip_Flop d_ff_1 (.D(rst), .clk(clk), .Q(d_ff_1_q));  // open: Qn, preset, reset
  Register #(.width(32)) register_1 (.D(a), .en(1'b1), .clk(clk), .Q(register_1_q));  // open: clr
  Register #(.width(32)) register_2 (.D(b), .en(1'b1), .clk(clk), .Q(register_2_q));  // open: clr
  not not_1 (not_1_out, comparator_3_eq);
  Comparator #(.mode("unsigned"), .width(32)) comparator_1 (
    .a(register_1_q), .b(a), .eq(comparator_1_eq));  // open: gt, lt
  Comparator #(.mode("unsigned"), .width(32)) comparator_2 (
    .a(register_2_q), .b(b), .eq(comparator_2_eq));  // open: gt, lt
  Comparator #(.mode("unsigned"), .width(1)) comparator_3 (
    .a(rst), .b(d_ff_1_q), .eq(comparator_3_eq));  // open: gt, lt
  not not_2 (not_2_out, comparator_1_eq);
  not not_3 (not_3_out, comparator_2_eq);
  D_Flip_Flop d_ff_2 (.D(donekosh), .clk(clk), .Q(d_ff_2_q));  // open: Qn, preset, reset
  D_Flip_Flop d_ff_3 (.D(or_1_out), .clk(clk), .Q(d_ff_3_q));  // open: Qn, preset, reset
  or or_1 (or_1_out, not_1_out, d_ff_2_q);
  or or_2 (donekosh, not_2_out, not_3_out);
  or or_3 (strt, d_ff_3_q, or_1_out);
endmodule
